// Logisim project FINAL1.circ as structural Verilog: 1 circuit, main circuit main
module main (
  input  [2:0] in_1,
  input  [2:0] in_2,
  input  [2:0] in_3,
  input  [7:0] in_4,
  input  in_5,
  input  in_6,
  input  in_7,
  input  in_8,
  input  Read_Write,
  input  [7:0] _0_ADD,
  input  in_11,
  input  [7:0] Immediate_Value,
  output [7:0] out_13
);

  wire and_1_out, and_2_out, and_3_out, and_4_out, and_5_out, and_6_out, and_7_out, and_8_out, clock_1_out,
       clock_2_out, clock_3_out, clock_4_out, clock_5_out, clock_6_out, clock_7_out, decoder_1_out0,
       decoder_1_out1, decoder_1_out2, decoder_1_out3, decoder_1_out4, decoder_1_out5, decoder_1_out6,
       decoder_1_out7;
  wire [7:0] adder_1_out, and_9_out, InA, InB, multiplexer_1_out, multiplexer_2_out, multiplexer_3_out,
       multiplexer_4_out, multiplexer_5_out, multiplexer_6_out, multiplexer_7_out, ram_1_data, register_1_q,
       register_2_q, register_3_q, register_4_q, register_5_q, register_6_q, register_7_q, register_8_q,
       register_9_q, RZ_q;

  Multiplexer #(.width(8)) multiplexer_1 (.in0(in_4), .in1(out_13), .out(multiplexer_1_out), .sel(in_5));  // open: en
  Decoder #(.select(3), .enable("false")) decoder_1 (
    .out0(decoder_1_out0), .out1(decoder_1_out1), .out2(decoder_1_out2), .out3(decoder_1_out3),
    .out4(decoder_1_out4), .out5(decoder_1_out5), .out6(decoder_1_out6), .out7(decoder_1_out7), .sel(in_1));
  and and_1 (and_1_out, decoder_1_out0, Read_Write);
  and and_2 (and_2_out, decoder_1_out1, Read_Write);
  and and_3 (and_3_out, decoder_1_out2, Read_Write);
  and and_4 (and_4_out, decoder_1_out3, Read_Write);
  and and_5 (and_5_out, decoder_1_out4, Read_Write);
  and and_6 (and_6_out, decoder_1_out5, Read_Write);
  and and_7 (and_7_out, decoder_1_out6, Read_Write);
  and and_8 (and_8_out, decoder_1_out7, Read_Write);
  Clock clock_1 (.out(clock_1_out));
  Register register_1 (.D(multiplexer_1_out), .en(and_1_out), .Q(register_1_q), .clk(clock_1_out));  // open: clr
  Register register_2 (.D(multiplexer_1_out), .en(and_2_out), .Q(register_2_q), .clk(clock_1_out));  // open: clr
  Register register_3 (.D(multiplexer_1_out), .en(and_3_out), .Q(register_3_q), .clk(clock_1_out));  // open: clr
  Register register_4 (.D(multiplexer_1_out), .en(and_4_out), .Q(register_4_q), .clk(clock_1_out));  // open: clr
  Register register_5 (.D(multiplexer_1_out), .en(and_5_out), .Q(register_5_q), .clk(clock_1_out));  // open: clr
  Register register_6 (.D(multiplexer_1_out), .en(and_6_out), .Q(register_6_q), .clk(clock_1_out));  // open: clr
  Register register_7 (.D(multiplexer_1_out), .en(and_7_out), .Q(register_7_q), .clk(clock_1_out));  // open: clr
  Register register_8 (.D(multiplexer_1_out), .en(and_8_out), .Q(register_8_q), .clk(clock_1_out));  // open: clr
  Multiplexer #(.select(3), .width(8)) multiplexer_2 (
    .in0(register_1_q), .in1(register_2_q), .in2(register_3_q), .in3(register_4_q), .in4(register_5_q),
    .in5(register_6_q), .in6(register_7_q), .in7(register_8_q), .out(multiplexer_2_out), .sel(in_2));  // open: en
  Multiplexer #(.select(3), .width(8)) multiplexer_3 (
    .in0(register_1_q), .in1(register_2_q), .in2(register_3_q), .in3(register_4_q), .in4(register_5_q),
    .in5(register_6_q), .in6(register_7_q), .in7(register_8_q), .out(multiplexer_3_out), .sel(in_3));  // open: en
  Register RA (.D(multiplexer_2_out), .Q(InA), .clk(clock_2_out));  // open: en, clr
  Clock clock_2 (.out(clock_2_out));
  Register RB (.D(multiplexer_3_out), .Q(InB), .clk(clock_3_out));  // open: en, clr
  Clock clock_3 (.out(clock_3_out));
  Multiplexer #(.width(8)) multiplexer_4 (
    .in0(InB), .in1(Immediate_Value), .out(multiplexer_4_out), .sel(in_11));  // open: en
  Register register_9 (.D(InB), .Q(register_9_q), .clk(clock_4_out));  // open: en, clr
  Clock clock_4 (.out(clock_4_out));
  Adder adder_1 (.a(InA), .b(multiplexer_4_out), .out(adder_1_out));  // open: cin, cout
  assign and_9_out = InA & multiplexer_4_out;  // AND_Gate and_9, 8 bits wide
  Multiplexer #(.width(8), .enable("false")) multiplexer_5 (
    .in0(adder_1_out), .in1(and_9_out), .out(multiplexer_5_out), .sel(in_6));
  Multiplexer #(.width(8), .enable("false")) multiplexer_6 (
    .in0(multiplexer_5_out), .in1(_0_ADD), .out(multiplexer_6_out), .sel(in_7));
  Register RZ (.D(multiplexer_6_out), .Q(RZ_q), .clk(clock_5_out));  // open: en, clr
  Clock clock_5 (.out(clock_5_out));
  RAM #(.bus("separate")) ram_1 (
    .addr(RZ_q), .din(register_9_q), .data(ram_1_data), .clk(clock_6_out));  // open: str, sel, ld, clr
  Clock clock_6 (.out(clock_6_out));
  Multiplexer #(.width(8), .enable("false")) multiplexer_7 (
    .in0(RZ_q), .in1(ram_1_data), .out(multiplexer_7_out), .sel(in_8));
  Register register_10 (.D(multiplexer_7_out), .Q(out_13), .clk(clock_7_out));  // open: en, clr
  Clock clock_7 (.out(clock_7_out));

  // Other names for the same wires on the sheet: IV[7:0] = Immediate_Value; R_W = Read_Write; RY[7:0] = out_13

  // Notes on the sheet:
  //   Write Register 
  //   Select Lines For MUX1
  //   Select Lines For MUX2
  //   Input  
  //   0-Write Data From Input  
  //   1-Write Output Into Destination Register  
  //   Output
  //   R0
  //   R1
  //   R2
  //   R3
  //   R4
  //   R5
  //   R6
  //   R7
  //   REGISTER FILE
  //   MUX1
  //   MUX2
  //   Immediate Value
  //   MUXA
  //   0-RA
  //   Intermediate Registers
  //   RM
  //   Adder
  //   AND
  //   ALU
  //   1-AND
  //   Memory Address
  //   MEMORY
  //   MUXY
  //   RY
  //   Memory Data
endmodule
