// Logisim project circuit_final.circ as structural Verilog: 7 circuits, main circuit main
module main (
  input  [3:0] in_1,
  input  [3:0] in_2,
  input  [3:0] in_3,
  input  in_4,
  input  [9:0] RB,
  input  in_6,
  input  enable,
  input  load_store_prime,
  input  F_N,
  input  in_10,
  input  Load_to_shifter,
  input  reset,
  input  [1:0] in_13,
  output [9:0] out_14,
  output [1:0] Last_values,
  output [9:0] out_16
);

  wire clock_1_out, clock_2_out;
  wire [4:0] address, bit_shrinker_1_out_2, bit_shrinker_2_out_2;
  wire [9:0] data_in, multiplexer_1_out, multiplexer_2_out, processor_registers_1_ra_2,
       processor_registers_1_rb_2, register_1_o_p, register_2_o_p, Return_address, rz_1_out_3, rz_2_out_3;

  Clock clock_1 (.out(clock_1_out));
  Clock clock_2 (.out(clock_2_out));
  Processor_registers processor_registers_1 (
    .WRITE_DATA(rz_2_out_3), .RA_2(processor_registers_1_ra_2), .RB_2(processor_registers_1_rb_2),
    .WRITE_ADDRESS(in_2), .R_W_prime(in_4), .in_5(clock_1_out), .RA(in_1), .RB(in_3));
  Register register_1 (.ip(processor_registers_1_ra_2), .o_p(register_1_o_p), .in_2(clock_1_out));
  Bit_Shrinker bit_shrinker_1 (.in_1(register_1_o_p), .out_2(bit_shrinker_1_out_2));
  ALU alu_1 (
    .Multiplicand(bit_shrinker_1_out_2), .First(F_N), .LOAD_shifter(Load_to_shifter), .in_6(reset),
    .B(bit_shrinker_2_out_2), .out_8(Last_values), .in_5(clock_2_out), .out_9(out_16), .in_7(in_10));
  RZ rz_1 (.in_1(out_16), .out_3(rz_1_out_3), .in_2(clock_1_out));
  Multiplexer #(.select(2), .width(10), .enable("false")) multiplexer_1 (
    .in0(rz_1_out_3), .in1(out_14), .in2(Return_address), .out(multiplexer_1_out), .sel(in_13));  // open: in3
  RZ rz_2 (.in_1(multiplexer_1_out), .out_3(rz_2_out_3), .in_2(clock_1_out));
  Register register_2 (.ip(processor_registers_1_rb_2), .o_p(register_2_o_p), .in_2(clock_1_out));
  Multiplexer #(.width(10), .enable("false")) multiplexer_2 (
    .in0(register_2_o_p), .in1(RB), .out(multiplexer_2_out), .sel(in_6));
  Bit_Shrinker bit_shrinker_2 (.in_1(multiplexer_2_out), .out_2(bit_shrinker_2_out_2));
  Bit_Shrinker bit_shrinker_3 (.in_1(rz_1_out_3), .out_2(address));
  Register register_3 (.ip(processor_registers_1_rb_2), .o_p(data_in), .in_2(clock_1_out));
  RAM ram_1 (
    .Address(address), .DataIN(data_in), .Load_Store_prime(load_store_prime), .Clock(clock_1_out),
    .o_p(out_14), .select(enable));

  // Other names for the same wires on the sheet: Load_data[9:0] = out_14

  // Notes on the sheet:
  //   RA
  //   RZ
  //   RY
  //   10110 x 10011
endmodule

module Register (
  input  [9:0] ip,
  input  in_2,
  output [9:0] o_p
);

  Register_part #(.width(10)) register_1 (.D(ip), .Q(o_p), .clk(in_2));  // open: en, clr
endmodule

module RAM (
  input  [4:0] Address,
  input  [9:0] DataIN,
  input  Load_Store_prime,
  input  Clock,
  input  select,
  output [9:0] o_p
);

  wire not_1_out;
  wire [9:0] ram_1_data;

  not not_1 (not_1_out, Load_Store_prime);
  Register_part #(.width(10)) register_1 (.D(ram_1_data), .Q(o_p), .clk(Clock));  // open: en, clr
  RAM_part #(.addrWidth(5), .dataWidth(10), .bus("separate")) ram_1 (
    .addr(Address), .din(DataIN), .data(ram_1_data), .str(not_1_out), .sel(select), .clk(Clock),
    .ld(Load_Store_prime));  // open: clr
endmodule

module ALU (
  input  [4:0] B,
  input  [4:0] Multiplicand,
  input  First,
  input  LOAD_shifter,
  input  in_5,
  input  in_6,
  input  in_7,
  output [1:0] out_8,
  output [9:0] out_9
);

  wire [4:0] adder_2_out, multiplexer_1_out, multiplexer_3_out, shift_register_1_q4;
  wire [4:1] shift_register_1_q8;
  wire [9:0] bit_extender_1_out, multiplexer_2_out;
  wire [9:5] adder_1_out, subtractor_1_out;

  Multiplexer #(.width(5), .enable("false")) multiplexer_1 (
    .in0({5{1'b0}}), .in1(shift_register_1_q4), .out(multiplexer_1_out), .sel(First));
  Multiplexer #(.select(2), .width(10), .enable("false")) multiplexer_2 (
    .in0({multiplexer_1_out, multiplexer_3_out}), .in1({adder_1_out, multiplexer_3_out}),
    .in2({subtractor_1_out, multiplexer_3_out}), .in3({multiplexer_1_out, multiplexer_3_out}),
    .out(multiplexer_2_out), .sel(out_8));
  Shift_Register #(.length(11)) shift_register_1 (
    .shift(1'b1), .in(shift_register_1_q4[4]), .clk(in_5), .load(LOAD_shifter), .clr(in_6),
    .d0(multiplexer_2_out[9]), .q0(shift_register_1_q4[4]), .d1(multiplexer_2_out[8]),
    .q1(shift_register_1_q4[3]), .d2(multiplexer_2_out[7]), .q2(shift_register_1_q4[2]),
    .d3(multiplexer_2_out[6]), .q3(shift_register_1_q4[1]), .d4(multiplexer_2_out[5]),
    .q4(shift_register_1_q4[0]), .d5(multiplexer_2_out[4]), .q5(shift_register_1_q8[4]),
    .d6(multiplexer_2_out[3]), .q6(shift_register_1_q8[3]), .d7(multiplexer_2_out[2]),
    .q7(shift_register_1_q8[2]), .d8(multiplexer_2_out[1]), .q8(shift_register_1_q8[1]),
    .d9(multiplexer_2_out[0]), .q9(out_8[1]), .d10(1'b0), .q10(out_8[0]));  // open: out
  Multiplexer #(.width(5), .enable("false")) multiplexer_3 (
    .in0(B), .in1({shift_register_1_q8, out_8[1]}), .out(multiplexer_3_out), .sel(First));
  Subtractor #(.width(5)) subtractor_1 (
    .a(multiplexer_1_out), .b(Multiplicand), .out(subtractor_1_out));  // open: bin, bout
  Adder #(.width(5)) adder_1 (.a(multiplexer_1_out), .b(Multiplicand), .out(adder_1_out));  // open: cin, cout
  assign bit_extender_1_out = {{5{1'b0}}, adder_2_out};  // Bit_Extender bit_extender_1
  Multiplexer #(.width(10), .enable("false")) multiplexer_4 (
    .in0({shift_register_1_q4, shift_register_1_q8, out_8[1]}), .in1(bit_extender_1_out), .out(out_9),
    .sel(in_7));
  Adder #(.width(5)) adder_2 (.a(Multiplicand), .b(B), .out(adder_2_out));  // open: cin, cout
endmodule

module RZ (
  input  [9:0] in_1,
  input  in_2,
  output [9:0] out_3
);

  Register_part #(.width(10)) register_1 (.D(in_1), .Q(out_3), .clk(in_2));  // open: en, clr
endmodule

module Processor_registers (
  input  [3:0] RA,
  input  [3:0] WRITE_ADDRESS,
  input  [3:0] RB,
  input  [9:0] WRITE_DATA,
  input  in_5,
  input  R_W_prime,
  output [9:0] RA_2,
  output [9:0] RB_2
);

  wire and_1_out, and_2_out, and_3_out, and_4_out, and_5_out, and_6_out, and_7_out, and_8_out, and_9_out,
       and_10_out, and_11_out, and_12_out, and_13_out, and_14_out, and_15_out, and_16_out, decoder_1_out0,
       decoder_1_out1, decoder_1_out2, decoder_1_out3, decoder_1_out4, decoder_1_out5, decoder_1_out6,
       decoder_1_out7, decoder_1_out8, decoder_1_out9, decoder_1_out10, decoder_1_out11, decoder_1_out12,
       decoder_1_out13, decoder_1_out14, decoder_1_out15;
  wire [9:0] register_1_q, register_2_q, register_3_q, register_4_q, register_5_q, register_6_q,
       register_7_q, register_8_q, register_9_q, register_10_q, register_11_q, register_12_q, register_13_q,
       register_14_q, register_15_q, register_16_q;

  Decoder #(.select(4), .enable("false")) decoder_1 (
    .out0(decoder_1_out0), .out1(decoder_1_out1), .out2(decoder_1_out2), .out3(decoder_1_out3),
    .out4(decoder_1_out4), .out5(decoder_1_out5), .out6(decoder_1_out6), .out7(decoder_1_out7),
    .out8(decoder_1_out8), .out9(decoder_1_out9), .out10(decoder_1_out10), .out11(decoder_1_out11),
    .out12(decoder_1_out12), .out13(decoder_1_out13), .out14(decoder_1_out14), .out15(decoder_1_out15),
    .sel(WRITE_ADDRESS));
  and and_1 (and_1_out, decoder_1_out0, R_W_prime);
  and and_2 (and_2_out, decoder_1_out4, R_W_prime);
  and and_3 (and_3_out, decoder_1_out8, R_W_prime);
  and and_4 (and_4_out, decoder_1_out12, R_W_prime);
  Register_part #(.width(10)) register_1 (.D(WRITE_DATA), .en(and_1_out), .Q(register_1_q), .clk(in_5));  // open: clr
  Register_part #(.width(10)) register_2 (.D(WRITE_DATA), .en(and_2_out), .Q(register_2_q), .clk(in_5));  // open: clr
  Register_part #(.width(10)) register_3 (.D(WRITE_DATA), .en(and_3_out), .Q(register_3_q), .clk(in_5));  // open: clr
  Register_part #(.width(10)) register_4 (.D(WRITE_DATA), .en(and_4_out), .Q(register_4_q), .clk(in_5));  // open: clr
  and and_5 (and_5_out, decoder_1_out1, R_W_prime);
  and and_6 (and_6_out, decoder_1_out5, R_W_prime);
  and and_7 (and_7_out, decoder_1_out9, R_W_prime);
  and and_8 (and_8_out, decoder_1_out13, R_W_prime);
  Register_part #(.width(10)) register_5 (.D(WRITE_DATA), .en(and_5_out), .Q(register_5_q), .clk(in_5));  // open: clr
  Register_part #(.width(10)) register_6 (.D(WRITE_DATA), .en(and_6_out), .Q(register_6_q), .clk(in_5));  // open: clr
  Register_part #(.width(10)) register_7 (.D(WRITE_DATA), .en(and_7_out), .Q(register_7_q), .clk(in_5));  // open: clr
  Register_part #(.width(10)) register_8 (.D(WRITE_DATA), .en(and_8_out), .Q(register_8_q), .clk(in_5));  // open: clr
  and and_9 (and_9_out, decoder_1_out2, R_W_prime);
  and and_10 (and_10_out, decoder_1_out6, R_W_prime);
  and and_11 (and_11_out, decoder_1_out10, R_W_prime);
  and and_12 (and_12_out, decoder_1_out14, R_W_prime);
  Register_part #(.width(10)) register_9 (.D(WRITE_DATA), .en(and_9_out), .Q(register_9_q), .clk(in_5));  // open: clr
  Register_part #(.width(10)) register_10 (
    .D(WRITE_DATA), .en(and_10_out), .Q(register_10_q), .clk(in_5));  // open: clr
  Register_part #(.width(10)) register_11 (
    .D(WRITE_DATA), .en(and_11_out), .Q(register_11_q), .clk(in_5));  // open: clr
  Register_part #(.width(10)) register_12 (
    .D(WRITE_DATA), .en(and_12_out), .Q(register_12_q), .clk(in_5));  // open: clr
  and and_13 (and_13_out, decoder_1_out3, R_W_prime);
  and and_14 (and_14_out, decoder_1_out7, R_W_prime);
  and and_15 (and_15_out, decoder_1_out11, R_W_prime);
  and and_16 (and_16_out, decoder_1_out15, R_W_prime);
  Register_part #(.width(10)) register_13 (
    .D(WRITE_DATA), .en(and_13_out), .Q(register_13_q), .clk(in_5));  // open: clr
  Register_part #(.width(10)) register_14 (
    .D(WRITE_DATA), .en(and_14_out), .Q(register_14_q), .clk(in_5));  // open: clr
  Register_part #(.width(10)) register_15 (
    .D(WRITE_DATA), .en(and_15_out), .Q(register_15_q), .clk(in_5));  // open: clr
  Register_part #(.width(10)) register_16 (
    .D(WRITE_DATA), .en(and_16_out), .Q(register_16_q), .clk(in_5));  // open: clr
  Multiplexer #(.select(4), .width(10), .enable("false")) multiplexer_1 (
    .in0(register_1_q), .in1(register_5_q), .in2(register_9_q), .in3(register_13_q), .in4(register_2_q),
    .in5(register_6_q), .in6(register_10_q), .in7(register_14_q), .in8(register_3_q), .in9(register_7_q),
    .in10(register_11_q), .in11(register_15_q), .in12(register_4_q), .in13(register_8_q),
    .in14(register_12_q), .in15(register_16_q), .out(RA_2), .sel(RA));
  Multiplexer #(.select(4), .width(10), .enable("false")) multiplexer_2 (
    .in0(register_1_q), .in1(register_5_q), .in2(register_9_q), .in3(register_13_q), .in4(register_2_q),
    .in5(register_6_q), .in6(register_10_q), .in7(register_14_q), .in8(register_3_q), .in9(register_7_q),
    .in10(register_11_q), .in11(register_15_q), .in12(register_4_q), .in13(register_8_q),
    .in14(register_12_q), .in15(register_16_q), .out(RB_2), .sel(RB));
endmodule

module Bit_Shrinker (
  input  [9:0] in_1,
  output [4:0] out_2
);

  Bit_Extender #(.in_width(10), .out_width(5)) bit_extender_1 (.in(in_1), .out(out_2));
endmodule
